// Logisim project s-mips.circ as structural Verilog
module S_MIPS_Board (
  input  DESHABILITAR_DISPATCHER,
  output halt
);

  wire button_1_out, CLK, CS, d_ff_1_q, LCLR, LoadRAM, LoadRAMOn, LW, R_R_W, R_W, ram_dispatcher_1_finished,
       RCS, Reset_out, RST, TTY_EN;
  wire [2:0] KDB;
  wire [3:0] LMask, Mask, ram_1_read_time, ram_1_write_time, RMask;
  wire [6:0] KDB_DATA, TTY_DATA;
  wire [15:0] Addr, LAddr, RAddr;
  wire [31:0] I0, I1, I2, I3, LData, ram_1_data_out_0, ram_1_data_out_1, ram_1_data_out_2, ram_1_data_out_3,
       RI0, RI1, RI2, RI3;

  TTY #(.rows(25), .cols(80)) tty_1 (.data(TTY_DATA), .clk(CLK), .we(TTY_EN), .clr(RST));
  not not_1 (LoadRAMOn, ram_dispatcher_1_finished);
  RAM_Dispatcher ram_dispatcher_1 (
    .WriteTime(ram_1_write_time), .Clock(CLK), .Data(LData), .Address(LAddr), .Mask(LMask),
    .Finished(ram_dispatcher_1_finished), .Write(LW), .CLR(LCLR));
  Keyboard #(.buflen(64)) keyboard_1 (.clk(CLK), .re(KDB[0]), .avail(KDB[2]), .data(KDB_DATA));  // open: clr
  RAM ram_1 (
    .Address(RAddr), .Data_Out_0(ram_1_data_out_0), .Data_Out_1(ram_1_data_out_1),
    .Data_Out_2(ram_1_data_out_2), .Data_Out_3(ram_1_data_out_3), .Data_In_0(RI0), .Data_In_1(RI1),
    .Data_In_2(RI2), .Data_In_3(RI3), .Mask(RMask), .nRead_Write(R_R_W), .Chip_Select(RCS),
    .Read_Time(ram_1_read_time), .Reset(button_1_out), .Write_Time(ram_1_write_time));
  Button button_1 (.out(button_1_out));
  D_Flip_Flop d_ff_1 (.clk(CLK), .D(1'b1), .Q(d_ff_1_q), .reset(Reset_out));  // open: Qn, preset, en
  Button Reset (.out(Reset_out));
  S_MIPS s_mips_1 (
    .Kbd_Enable(KDB[0]), .Address(Addr), .Kbd_Clear(KDB[1]), .Kbd_Available(KDB[2]), .RAM_In_0(I0),
    .Kbd_ASCII_Data(KDB_DATA), .RAM_In_1(I1), .TTY_Enable(TTY_EN), .RAM_In_2(I2), .RAM_In_3(I3),
    .TTY_ASCII_Data(TTY_DATA), .Reset(RST), .RAM_Out_0(ram_1_data_out_0), .Clock(CLK),
    .RAM_Out_1(ram_1_data_out_1), .Stop(halt), .RAM_Out_2(ram_1_data_out_2), .RAM_Out_3(ram_1_data_out_3),
    .Mask(Mask), .Read_Time(ram_1_read_time), .Write_Time(ram_1_write_time), .nRead_Write(R_W),
    .Chip_Select(CS));
  D_Flip_Flop d_ff_2 (.clk(CLK), .D(d_ff_1_q), .Qn(LCLR), .reset(Reset_out));  // open: Q, preset, en
  or or_1 (RST, LCLR, LoadRAM);
  Clock clock_1 (.out(CLK));
  Multiplexer #(.width(32), .enable("false")) multiplexer_1 (.in0(I0), .in1(LData), .out(RI0), .sel(LoadRAM));
  Multiplexer #(.width(32), .enable("false")) multiplexer_2 (.in0(I1), .in1(LData), .out(RI1), .sel(LoadRAM));
  Multiplexer #(.width(32), .enable("false")) multiplexer_3 (.in0(I2), .in1(LData), .out(RI2), .sel(LoadRAM));
  Multiplexer #(.width(32), .enable("false")) multiplexer_4 (.in0(I3), .in1(LData), .out(RI3), .sel(LoadRAM));
  and and_1 (LoadRAM, ~DESHABILITAR_DISPATCHER, LoadRAMOn);  // AND_Gate
  Multiplexer #(.width(16), .enable("false")) multiplexer_5 (.in0(Addr), .in1(LAddr), .out(RAddr), .sel(LoadRAM));
  Multiplexer #(.width(4), .enable("false")) multiplexer_6 (.in0(Mask), .in1(LMask), .out(RMask), .sel(LoadRAM));
  Multiplexer #(.enable("false")) multiplexer_7 (.in0(CS), .in1(LW), .out(RCS), .sel(LoadRAM));
  Multiplexer #(.enable("false")) multiplexer_8 (.in0(R_W), .in1(LW), .out(R_R_W), .sel(LoadRAM));

  // Notes on the sheet:
  //   NO MODIFICAR
  //   Keyboard
endmodule

module RAM (
  input  [15:0] Address,
  input  [31:0] Data_In_0,
  input  [31:0] Data_In_1,
  input  [31:0] Data_In_2,
  input  [31:0] Data_In_3,
  input  [3:0] Mask,
  input  nRead_Write,
  input  Chip_Select,
  input  Reset,
  output [31:0] Data_Out_0,
  output [31:0] Data_Out_1,
  output [31:0] Data_Out_2,
  output [31:0] Data_Out_3,
  output [3:0] Read_Time,
  output [3:0] Write_Time
);

  wire and_2_out, and_3_out, and_4_out, and_5_out, and_6_out, and_7_out, and_8_out, and_9_out, Changed, CLK,
       comparator_2_eq, comparator_3_eq, comparator_4_eq, comparator_5_eq, comparator_6_eq, Count,
       demultiplexer_3_out0, Idle, Idle_q, Load, Load0, Load1, nand_1_out, or_1_out, or_2_out, or_3_out,
       or_4_out, or_5_out, or_6_out, or_7_out, or_8_out, or_9_out, or_10_out, Proc_q, Update_Mem, Zero_Time;
  wire [3:0] counter_1_q, multiplexer_1_out, subtractor_1_out;
  wire [31:0] register_1_q, register_2_q, register_3_q, register_4_q, register_5_q;

  // Probe on 4'b0011
  // Probe on 4'b0010
  Multiplexer #(.width(4), .enable("false")) multiplexer_1 (
    .in0(4'b0011), .in1(4'b0010), .out(multiplexer_1_out), .sel(nRead_Write));
  or or_1 (or_1_out, Idle, Update_Mem);
  or or_2 (or_2_out, ~Chip_Select, Reset);  // OR_Gate
  Subtractor #(.width(4)) subtractor_1 (.a(multiplexer_1_out), .b(4'b0010), .out(subtractor_1_out));  // open: bin, bout
  Demultiplexer #(.enable("false")) demultiplexer_1 (.out0(Idle), .out1(Load0), .in(Idle_q), .sel(Changed));
  D_Flip_Flop u_Idle (.clk(CLK), .D(or_1_out), .Q(Idle_q), .preset(or_2_out));  // open: Qn, en, reset
  // Probe on counter_1_q
  Counter #(.width(4), .max('hf)) counter_1 (
    .load(Load), .D(subtractor_1_out), .count(Count), .Q(counter_1_q), .clk(CLK), .clr(or_3_out));  // open: carry
  or or_3 (or_3_out, ~Chip_Select, Reset);  // OR_Gate
  Comparator #(.width(4), .mode("unsigned")) comparator_1 (
    .a(4'b0000), .b(counter_1_q), .eq(Zero_Time));  // open: gt, lt
  or or_4 (or_4_out, Count, Load0, Load1);
  Register #(.width(32)) register_1 (.D(Data_In_0), .en(Chip_Select), .Q(register_1_q), .clk(CLK), .clr(or_5_out));
  or or_5 (or_5_out, ~Chip_Select, Reset);  // OR_Gate
  Register #(.width(32)) register_2 (.D(Data_In_1), .en(Chip_Select), .Q(register_2_q), .clk(CLK), .clr(or_6_out));
  or or_6 (or_6_out, ~Chip_Select, Reset);  // OR_Gate
  Register #(.width(32)) register_3 (.D(Data_In_2), .en(Chip_Select), .Q(register_3_q), .clk(CLK), .clr(or_7_out));
  or or_7 (or_7_out, ~Chip_Select, Reset);  // OR_Gate
  Register #(.width(32)) register_4 (.D(Data_In_3), .en(Chip_Select), .Q(register_4_q), .clk(CLK), .clr(or_8_out));
  or or_8 (or_8_out, ~Chip_Select, Reset);  // OR_Gate
  Register #(.width(32)) register_5 (
    .D({{11{1'b1}}, nRead_Write, Mask, Address}), .en(Chip_Select), .Q(register_5_q), .clk(CLK),
    .clr(or_9_out));
  or or_9 (or_9_out, ~Chip_Select, Reset);  // OR_Gate
  D_Flip_Flop Proc (.clk(CLK), .D(or_4_out), .Q(Proc_q), .reset(or_10_out));  // open: Qn, preset, en
  or or_10 (or_10_out, ~Chip_Select, Reset);  // OR_Gate
  Demultiplexer #(.enable("false")) demultiplexer_2 (
    .out0(Count), .out1(Update_Mem), .in(demultiplexer_3_out0), .sel(Zero_Time));
  Demultiplexer #(.enable("false")) demultiplexer_3 (
    .out0(demultiplexer_3_out0), .out1(Load1), .in(Proc_q), .sel(Changed));
  Clock clock_1 (.out(CLK));
  Comparator #(.width(32)) comparator_2 (.a(register_1_q), .b(Data_In_0), .eq(comparator_2_eq));  // open: gt, lt
  Comparator #(.width(32)) comparator_3 (.a(register_2_q), .b(Data_In_1), .eq(comparator_3_eq));  // open: gt, lt
  Comparator #(.width(32)) comparator_4 (.a(register_3_q), .b(Data_In_2), .eq(comparator_4_eq));  // open: gt, lt
  Comparator #(.width(32)) comparator_5 (.a(register_4_q), .b(Data_In_3), .eq(comparator_5_eq));  // open: gt, lt
  Comparator #(.width(32)) comparator_6 (
    .a(register_5_q), .b({{11{1'b1}}, nRead_Write, Mask, Address}), .eq(comparator_6_eq));  // open: gt, lt
  nand nand_1 (nand_1_out, comparator_6_eq, comparator_2_eq, comparator_3_eq, comparator_4_eq, comparator_5_eq);
  and and_1 (Changed, nand_1_out, Chip_Select);
  or or_11 (Load, Count, Load1, Load0);
  and and_2 (and_2_out, Mask[0], Update_Mem, nRead_Write);
  and and_3 (and_3_out, Mask[1], Update_Mem, nRead_Write);
  and and_4 (and_4_out, Mask[2], Update_Mem, nRead_Write);
  and and_5 (and_5_out, Mask[3], Update_Mem, nRead_Write);
  RAM_part #(.addrWidth(16), .dataWidth(32), .bus("separate")) ram_1 (
    .addr(Address), .din(Data_In_0), .data(Data_Out_0), .str(and_2_out), .sel(Chip_Select), .clk(CLK),
    .ld(and_6_out), .clr(Reset));
  and and_6 (and_6_out, ~nRead_Write, Idle);  // AND_Gate
  RAM_part #(.addrWidth(16), .dataWidth(32), .bus("separate")) ram_2 (
    .addr(Address), .din(Data_In_1), .data(Data_Out_1), .str(and_3_out), .sel(Chip_Select), .clk(CLK),
    .ld(and_7_out), .clr(Reset));
  and and_7 (and_7_out, ~nRead_Write, Idle);  // AND_Gate
  RAM_part #(.addrWidth(16), .dataWidth(32), .bus("separate")) ram_3 (
    .addr(Address), .din(Data_In_2), .data(Data_Out_2), .str(and_4_out), .sel(Chip_Select), .clk(CLK),
    .ld(and_8_out), .clr(Reset));
  and and_8 (and_8_out, ~nRead_Write, Idle);  // AND_Gate
  RAM_part #(.addrWidth(16), .dataWidth(32), .bus("separate")) ram_4 (
    .addr(Address), .din(Data_In_3), .data(Data_Out_3), .str(and_5_out), .sel(Chip_Select), .clk(CLK),
    .ld(and_9_out), .clr(Reset));
  and and_9 (and_9_out, ~nRead_Write, Idle);  // AND_Gate

  assign Read_Time = 4'b0011;
  assign Write_Time = 4'b0010;

  // Other names for the same wires on the sheet: M0 = Mask[0]; M1 = Mask[1]; M2 = Mask[2]; M3 = Mask[3];
  //   RW = nRead_Write; CLR = Reset; CS = Chip_Select; Load2 = Count

  // Notes on the sheet:
  //   NO MODIFICAR
  //   excepto quizás los valores RT y WT
  //   BANK0
  //   BANK1
  //   BANK2
  //   BANK3
endmodule

module RAM_Dispatcher (
  input  [3:0] WriteTime,
  input  Clock,
  input  CLR,
  output [31:0] Data,
  output [15:0] Address,
  output [3:0] Mask,
  output Finished,
  output Write
);

  wire demultiplexer_2_out1, demultiplexer_3_out1, End, IDLE_q, IncAddr, Load, or_1_out, or_2_out, While_q,
       WriteEnd;
  wire [3:0] counter_1_q;
  wire [31:0] CurrentAddress_q;

  Counter #(.width(32), .max('hffffffff)) CurrentAddress (
    .count(IncAddr), .Q({CurrentAddress_q[31:18], Address, CurrentAddress_q[1:0]}), .clk(Clock), .clr(CLR));  // open: load, D, carry
  or or_1 (or_1_out, IncAddr, demultiplexer_3_out1, Finished);
  D_Flip_Flop IDLE (.clk(Clock), .D(or_1_out), .Q(IDLE_q), .preset(CLR));  // open: Qn, en, reset
  Demultiplexer #(.enable("false")) demultiplexer_1 (.out0(Load), .out1(Finished), .in(IDLE_q), .sel(End));
  D_Flip_Flop While (.clk(Clock), .D(or_2_out), .Q(While_q), .reset(CLR));  // open: Qn, preset, en
  or or_2 (or_2_out, Write, Load);
  RAM_part #(.addrWidth(18), .dataWidth(32)) ram_1 (
    .addr({Address, CurrentAddress_q[1:0]}), .data(Data), .clk(Clock));  // open: sel, ld, clr
  Demultiplexer #(.enable("false")) demultiplexer_2 (
    .out0(Write), .out1(demultiplexer_2_out1), .in(While_q), .sel(WriteEnd));
  Decoder #(.select(2)) decoder_1 (
    .out0(Mask[0]), .out1(Mask[1]), .out2(Mask[2]), .out3(Mask[3]), .sel(CurrentAddress_q[1:0]));  // open: en
  Demultiplexer #(.enable("false")) demultiplexer_3 (
    .out0(IncAddr), .out1(demultiplexer_3_out1), .in(demultiplexer_2_out1), .sel(End));
  Counter #(.width(4), .max('hf)) counter_1 (
    .load(Load), .D(WriteTime), .count(Write), .Q(counter_1_q), .clk(Clock));  // open: carry, clr
  Comparator #(.width(32)) comparator_1 (.a(Data), .b({32{1'b1}}), .eq(End));  // open: gt, lt
  Comparator #(.width(4)) comparator_2 (.a(4'b0000), .b(counter_1_q), .eq(WriteEnd));  // open: gt, lt

  // Other names for the same wires on the sheet: CLK = Clock; Count = Write; WT[3:0] = WriteTime
endmodule

module S_MIPS (
  input  Kbd_Available,
  input  [6:0] Kbd_ASCII_Data,
  input  [31:0] RAM_Out_0,
  input  [31:0] RAM_Out_1,
  input  Reset,
  input  [31:0] RAM_Out_2,
  input  Clock,
  input  [31:0] RAM_Out_3,
  input  [3:0] Read_Time,
  input  [3:0] Write_Time,
  output Kbd_Enable,
  output [15:0] Address,
  output Kbd_Clear,
  output TTY_Enable,
  output [6:0] TTY_ASCII_Data,
  output Stop,
  output [31:0] RAM_In_0,
  output [31:0] RAM_In_1,
  output [31:0] RAM_In_2,
  output [31:0] RAM_In_3,
  output [3:0] Mask,
  output nRead_Write,
  output Chip_Select
);

  wire Control_Unit_e_inst, Control_Unit_e_pc, Control_Unit_read_end, Halt, PC_Address, Read_RAM, Write_RAM;
  wire [31:0] Dir_RAM, Value_Read, Value_Write;

  Write_To_RAM write_to_ram_1 (
    .RAM_Address(Dir_RAM), .ADDR(Address), .Mask(Mask), .Value(Value_Write), .Bank_0(RAM_In_0),
    .Bank_1(RAM_In_1), .Bank_2(RAM_In_2), .Bank_3(RAM_In_3));
  Control_Unit_2 Control_Unit (
    .Reset(Reset), .Read_RAM_Time(Read_Time), .Clock(Clock), .Write_RAM_Time(Write_Time),
    .Read_RAM(Read_RAM), .Write_RAM(Write_RAM), .halt(Halt), .E_inst(Control_Unit_e_inst), .CS(Chip_Select),
    .read_end(Control_Unit_read_end), .R_W(nRead_Write), .E_PC(Control_Unit_e_pc), .\end (Stop),
    .PC_Address(PC_Address));
  Read_From_RAM read_from_ram_1 (
    .RAM_Address(Dir_RAM), .Bank_0(RAM_Out_0), .Bank_1(RAM_Out_1), .Bank_2(RAM_Out_2), .Bank_3(RAM_Out_3),
    .Value(Value_Read));
  Data_Path_2 data_path_1 (
    .Clock(Clock), .Instruction(Value_Read), .Reset(Reset), .E_PC(Control_Unit_e_pc),
    .Read_RAM(Control_Unit_read_end), .E_inst(Control_Unit_e_inst), .Keyboard(Kbd_ASCII_Data),
    .KBD_AVAIL(Kbd_Available), .PC_Address(PC_Address), .Dir_Address(Dir_RAM), .RAM__w(Value_Write),
    .halt(Halt), .Read_RAM_2(Read_RAM), .kbd(Kbd_Enable), .Write_RAM(Write_RAM), .tty(TTY_Enable),
    .tty_DATA(TTY_ASCII_Data));

  assign Kbd_Clear = Reset;

  // Other names for the same wires on the sheet: CLK = Clock; CLR = Reset; CS = Chip_Select;
  //   KBD_AVAIL = Kbd_Available; KBD_DATA[6:0] = Kbd_ASCII_Data; RAM_A[15:0] = Address; RAM_INPUT_0[31:0] = RAM_In_0;
  //   RAM_INPUT_1[31:0] = RAM_In_1; RAM_INPUT_2[31:0] = RAM_In_2; RAM_INPUT_3[31:0] = RAM_In_3; RAM_MASK[3:0] = Mask;
  //   RAM_OUTPUT_0[31:0] = RAM_Out_0; RAM_OUTPUT_1[31:0] = RAM_Out_1; RAM_OUTPUT_2[31:0] = RAM_Out_2;
  //   RAM_OUTPUT_3[31:0] = RAM_Out_3; RW = nRead_Write; TTY_DATA[6:0] = TTY_ASCII_Data

  // Notes on the sheet:
  //   RAM ADDRESS
  //   DATA FROM RAM
  //   DATA TO RAM
  //   DATA WRITE MASK
  //   RAM TIMING
  //   RAM CONTROL
  //   KEYBOARD
  //   TTY
  //   SEQUENCING
endmodule

// Control \n Unit
module Control_Unit_2 (
  input  Reset,
  input  [3:0] Read_RAM_Time,
  input  Clock,
  input  [3:0] Write_RAM_Time,
  input  Read_RAM,
  input  Write_RAM,
  input  halt,
  output E_inst,
  output CS,
  output read_end,
  output R_W,
  output E_PC,
  output \end ,
  output PC_Address
);

  wire chip_1, chip_2, crono_1_finish, crono_2_finish, crono_rst_1, crono_rst_2, demultiplexer_1_out0,
       demultiplexer_2_out1, demultiplexer_3_out0, demultiplexer_4_out0, demultiplexer_4_out1,
       demultiplexer_5_out0, IDLE_q, Load_Inst_q, or_3_out, or_4_out, or_6_out, or_8_out, RAM, RAM_read_load;
  wire [3:0] multiplexer_1_out;

  or or_1 (RAM, Read_RAM, Write_RAM);
  or or_2 (E_PC, demultiplexer_5_out0, RAM_read_load);
  or or_3 (or_3_out, demultiplexer_5_out0, RAM_read_load, demultiplexer_2_out1);
  or or_4 (or_4_out, demultiplexer_1_out0, crono_rst_2);
  Multiplexer #(.width(4), .enable("false")) multiplexer_1 (
    .in0(Read_RAM_Time), .in1(Write_RAM_Time), .out(multiplexer_1_out), .sel(Write_RAM));
  D_Flip_Flop IDLE (.clk(Clock), .D(or_3_out), .Q(IDLE_q), .preset(Reset));  // open: Qn, en, reset
  Demultiplexer #(.enable("false")) demultiplexer_1 (
    .out0(demultiplexer_1_out0), .out1(read_end), .in(chip_2), .sel(crono_1_finish));
  D_Flip_Flop d_ff_1 (.clk(Clock), .D(or_4_out), .Q(chip_2), .reset(Reset));  // open: Qn, preset, en
  Crono crono_1 (.Time(multiplexer_1_out), .rest(crono_rst_2), .clock(Clock), .Finish(crono_1_finish));
  or or_5 (CS, chip_1, chip_2);
  Demultiplexer #(.enable("false")) demultiplexer_2 (
    .out0(crono_rst_1), .out1(demultiplexer_2_out1), .in(IDLE_q), .sel(Reset));
  D_Flip_Flop Load_Read (.clk(Clock), .D(read_end), .Q(RAM_read_load), .reset(Reset));  // open: Qn, preset, en
  D_Flip_Flop Read_Inst (.clk(Clock), .D(or_6_out), .Q(chip_1), .reset(Reset));  // open: Qn, preset, en
  or or_6 (or_6_out, demultiplexer_3_out0, crono_rst_1);
  or or_7 (PC_Address, chip_1, crono_rst_1, E_PC);
  Demultiplexer #(.enable("false")) demultiplexer_3 (
    .out0(demultiplexer_3_out0), .out1(E_inst), .in(chip_1), .sel(crono_2_finish));
  Crono crono_2 (.Time(Read_RAM_Time), .rest(crono_rst_1), .clock(Clock), .Finish(crono_2_finish));
  and and_1 (R_W, Write_RAM, chip_2);
  D_Flip_Flop Load_Inst (.clk(Clock), .D(E_inst), .Q(Load_Inst_q), .reset(Reset));  // open: Qn, preset, en
  Demultiplexer #(.enable("false")) demultiplexer_4 (
    .out0(demultiplexer_4_out0), .out1(demultiplexer_4_out1), .in(Load_Inst_q), .sel(halt));
  Demultiplexer #(.enable("false")) demultiplexer_5 (
    .out0(demultiplexer_5_out0), .out1(crono_rst_2), .in(demultiplexer_4_out0), .sel(RAM));
  or or_8 (or_8_out, demultiplexer_4_out1, \end );
  D_Flip_Flop u_Halt (.clk(Clock), .D(or_8_out), .Q(\end ), .reset(Reset));  // open: Qn, preset, en

  // Other names for the same wires on the sheet: clk = Clock; R_W_t = crono_rst_2; R_W_RAM = R_W;
  //   Read_Time[3:0] = Read_RAM_Time; rst = Reset; Write_Time[3:0] = Write_RAM_Time

  // Notes on the sheet:
  //   Inputs
  //   Outputs
endmodule

module Crono (
  input  [3:0] Time,
  input  rest,
  input  clock,
  output Finish
);

  wire [3:0] counter_1_q;

  Counter #(.width(4), .max('hf)) counter_1 (
    .count(1'b1), .Q(counter_1_q), .clk(clock), .clr(rest));  // open: load, D, carry
  Comparator #(.width(4)) comparator_1 (.a(Time), .b(counter_1_q), .eq(Finish));  // open: gt, lt

  // Notes on the sheet:
  //   Inputs
  //   Output
endmodule

module Data_Path_2 (
  input  Clock,
  input  [31:0] Instruction,
  input  Reset,
  input  E_PC,
  input  Read_RAM,
  input  E_inst,
  input  [6:0] Keyboard,
  input  KBD_AVAIL,
  input  PC_Address,
  output [31:0] Dir_Address,
  output [31:0] RAM__w,
  output halt,
  output Read_RAM_2,
  output kbd,
  output Write_RAM,
  output tty,
  output [6:0] tty_DATA
);

  wire add, addi, \and , and_1_out, and_2_out, andi, beq, bgtz, blez, bltz, bne, div, divu, E_HL, j, jr, lw,
       mfhi, mflo, mult, multu, Neg, nop, \nor , \or , or_1_out, or_2_out, or_3_out, or_4_out, or_5_out,
       or_7_out, or_8_out, or_11_out, ori, pop, push, R_W, rnd, slt, slti, sltu, sltui, sub, sw, tty_t,
       Type_I, \xor , xori, Zero;
  wire [3:0] ALU_Selector;
  wire [4:0] multiplexer_1_out, Rd, Rs, Rt;
  wire [15:0] cte;
  wire [25:0] Jump;
  wire [31:0] ALU_Output, B_C, bit_extender_2_out, cte_I15, Hi, High, Lo, multiplexer_2_out,
       multiplexer_4_out, PC, register_1_q, register_file_input_1_rf_input, Rt_t, SP;
  wire [31:7] Rs_t;

  or or_1 (or_1_out, add, sub, \and , \or );
  or or_2 (or_2_out, \nor , \xor , slt, sltu);
  or or_3 (or_3_out, mfhi, mflo, addi, andi);
  or or_4 (or_4_out, slti, ori, xori, sltui);
  or or_5 (or_5_out, rnd, kbd, E_HL);
  or or_6 (E_HL, mult, multu, div, divu);
  or or_7 (or_7_out, or_1_out, or_2_out, or_3_out, or_4_out, or_5_out);
  and and_1 (and_1_out, E_PC, or_7_out);
  or or_8 (or_8_out, lw, pop);
  and and_2 (and_2_out, or_8_out, Read_RAM);
  or or_9 (R_W, and_1_out, and_2_out);
  Register #(.width(32)) register_1 (.D(Instruction), .en(E_inst), .Q(register_1_q), .clk(Clock), .clr(Reset));
  Instruction_Decoder instruction_decoder_1 (
    .Instruction(register_1_q), .add(add), .\nor (\nor ), .pop(pop), .push(push), .halt(halt), .rnd(rnd),
    .addi(addi), .beq(beq), .j(j), .sub(sub), .\xor (\xor ), .tty(tty_t), .kbd(kbd), .andi(andi), .bne(bne),
    .mult(mult), .slt(slt), .ori(ori), .blez(blez), .mulu(multu), .sltu(sltu), .xori(xori), .bgtz(bgtz),
    .div(div), .mfhi(mfhi), .slti(slti), .bltz(bltz), .divu(divu), .mflo(mflo), .sltiu(sltui), .lw(lw),
    .\and (\and ), .nop(nop), .sw(sw), .\or (\or ), .jr(jr), .jump(Jump), .cte(cte), .Rs(Rs), .Rt(Rt),
    .Rd(Rd), .Tyoe_I(Type_I));
  Register_File_Input register_file_input_1 (
    .Random(rnd), .RAM(Instruction), .Kbd(kbd), .Move_From_High(mfhi), .ALU_Output(ALU_Output),
    .Move_From_Low(mflo), .Keyboard(Keyboard), .Pop(pop), .Load_Word(lw), .Clock(Clock), .High(Hi),
    .Keyboard_Avail(KBD_AVAIL), .Low(Lo), .RF_INPUT(register_file_input_1_rf_input));
  and and_3 (tty, tty_t, E_PC);
  Multiplexer #(.width(5), .enable("false")) multiplexer_1 (.in0(Rd), .in1(Rt), .out(multiplexer_1_out), .sel(Type_I));
  Register_File register_file_1 (
    .Data_Address(multiplexer_1_out), .Data_In(register_file_input_1_rf_input), .Output_A({Rs_t, tty_DATA}),
    .High(High), .Read_Write(R_W), .Select_A(Rs), .Select_B(Rt), .Clock(Clock), .Reset(Reset),
    .Enable_HL(E_HL), .Push(push), .Pop(pop), .Enable_Program_Counter(E_PC), .Output_B(Rt_t), .High_2(Hi),
    .Low(Lo), .Stack_Pointer(SP));
  Program_Counter program_counter_1 (
    .Branch_Control(B_C), .Instruction(PC), .Enabled(E_PC), .Clock(Clock), .Reset(Reset));
  ALU_Encoder alu_encoder_1 (
    .add(add), .\and (\and ), .slt(slt), .addi(addi), .andi(andi), .slti(slti), .\or (\or ), .sub(sub),
    .sltu(sltu), .orii(ori), .sltui(sltui), .div(div), .mult(mult), .\xor (\xor ), .\nor (\nor ),
    .divu(divu), .xorii(xori), .multu(multu), .ALU_Selector(ALU_Selector));
  Branch_Control branch_control_1 (
    .Branch_If_Equal(beq), .Program_Counter(PC), .Branch_If_Not_Equal(bne),
    .Branch_If__Less_Equal_Zero(blez), .Constant(cte), .Branch_If_Greater_Than_Zero(bgtz),
    .Branch_If_Less_Than_Zero(bltz), .Jump(Jump), .j(j), .Jump_Register(jr),
    .Source_Registration_1({Rs_t, tty_DATA}), .Source_Registration_2(Rt_t), .Next_Instruction(B_C));
  or or_10 (Write_RAM, sw, push);
  assign cte_I15 = {{16{cte[15]}}, cte};  // Bit_Extender bit_extender_1
  Multiplexer #(.width(32), .enable("false")) multiplexer_2 (
    .in0(cte_I15), .in1(bit_extender_2_out), .out(multiplexer_2_out), .sel(or_11_out));
  or or_11 (or_11_out, andi, ori, xori);
  assign bit_extender_2_out = {{16{1'b0}}, cte};  // Bit_Extender bit_extender_2
  Multiplexer #(.width(32), .enable("false")) multiplexer_3 (
    .in0({Rs_t, tty_DATA}), .in1(Rt_t), .out(RAM__w), .sel(sw));
  Multiplexer #(.width(32), .enable("false")) multiplexer_4 (
    .in0(Rt_t), .in1(multiplexer_2_out), .out(multiplexer_4_out), .sel(Type_I));
  or or_12 (Read_RAM_2, lw, pop);
  ALU alu_1 (
    .A_Data({Rs_t, tty_DATA}), .B_Data(multiplexer_4_out), .Selector(ALU_Selector), .Clock(Clock),
    .ALU_Output(ALU_Output), .High(High), .Zero_Flag(Zero), .Negative_Flag(Neg));
  RAM_Address ram_address_1 (
    .ALU(ALU_Output), .Stack_Pointer(SP), .Program_Counter(PC), .Store_Word(sw), .Load_Word(lw), .Pop(pop),
    .Push(push), .Program_Counter_Address(PC_Address), .Dir_RAM(Dir_Address));

  // Other names for the same wires on the sheet: Clk = Clock; Read__RAM = Read_RAM_2; Rs_t[6:0] = tty_DATA;
  //   Rst = Reset

  // Notes on the sheet:
  //   Inputs
  //   Outputs
endmodule

module Instruction_Decoder (
  input  [31:0] Instruction,
  output [25:0] jump,
  output [15:0] cte,
  output [4:0] Rs,
  output add,
  output \nor ,
  output pop,
  output push,
  output halt,
  output rnd,
  output addi,
  output beq,
  output j,
  output [4:0] Rt,
  output sub,
  output \xor ,
  output tty,
  output kbd,
  output andi,
  output bne,
  output [4:0] Rd,
  output mult,
  output slt,
  output ori,
  output blez,
  output mulu,
  output sltu,
  output xori,
  output bgtz,
  output Tyoe_I,
  output div,
  output mfhi,
  output slti,
  output bltz,
  output divu,
  output mflo,
  output sltiu,
  output lw,
  output \and ,
  output nop,
  output sw,
  output \or ,
  output jr
);

  wire _00_0000, _11_1000, _11_1111, comparator_5_eq, comparator_6_eq, comparator_7_eq, comparator_8_eq,
       comparator_13_eq, comparator_14_eq, comparator_15_eq, comparator_16_eq, comparator_22_eq,
       comparator_23_eq, comparator_24_eq, comparator_25_eq, comparator_30_eq, comparator_31_eq,
       comparator_32_eq, comparator_33_eq, comparator_34_eq, comparator_35_eq, comparator_36_eq,
       comparator_37_eq, comparator_38_eq, comparator_39_eq, or_1_out, or_2_out, or_3_out;

  Comparator #(.width(6)) comparator_1 (.a(Instruction[31:26]), .b({6{1'b0}}), .eq(_00_0000));  // open: gt, lt
  Comparator #(.width(6)) comparator_2 (.a(Instruction[31:26]), .b(6'b001000), .eq(addi));  // open: gt, lt
  Comparator #(.width(6)) comparator_3 (.a(Instruction[31:26]), .b(6'b001010), .eq(slti));  // open: gt, lt
  Comparator #(.width(6)) comparator_4 (.a(Instruction[31:26]), .b(6'b000110), .eq(blez));  // open: gt, lt
  Comparator #(.width(6)) comparator_5 (.a(Instruction[5:0]), .b(6'b100000), .eq(comparator_5_eq));  // open: gt, lt
  Comparator #(.width(6)) comparator_6 (.a(Instruction[5:0]), .b(6'b011010), .eq(comparator_6_eq));  // open: gt, lt
  Comparator #(.width(6)) comparator_7 (.a(Instruction[5:0]), .b(6'b100111), .eq(comparator_7_eq));  // open: gt, lt
  Comparator #(.width(6)) comparator_8 (.a(Instruction[5:0]), .b(6'b010000), .eq(comparator_8_eq));  // open: gt, lt
  and and_1 (add, _00_0000, comparator_5_eq);
  and and_2 (div, _00_0000, comparator_6_eq);
  and and_3 (\nor , _00_0000, comparator_7_eq);
  and and_4 (mfhi, _00_0000, comparator_8_eq);
  Comparator #(.width(6)) comparator_9 (.a(Instruction[31:26]), .b(6'b111000), .eq(_11_1000));  // open: gt, lt
  Comparator #(.width(6)) comparator_10 (.a(Instruction[31:26]), .b(6'b001100), .eq(andi));  // open: gt, lt
  Comparator #(.width(6)) comparator_11 (.a(Instruction[31:26]), .b(6'b001011), .eq(sltiu));  // open: gt, lt
  Comparator #(.width(6)) comparator_12 (.a(Instruction[31:26]), .b(6'b000111), .eq(bgtz));  // open: gt, lt
  Comparator #(.width(6)) comparator_13 (.a(Instruction[5:0]), .b(6'b100010), .eq(comparator_13_eq));  // open: gt, lt
  Comparator #(.width(6)) comparator_14 (.a(Instruction[5:0]), .b(6'b011011), .eq(comparator_14_eq));  // open: gt, lt
  Comparator #(.width(6)) comparator_15 (.a(Instruction[5:0]), .b(6'b101000), .eq(comparator_15_eq));  // open: gt, lt
  Comparator #(.width(6)) comparator_16 (.a(Instruction[5:0]), .b(6'b010010), .eq(comparator_16_eq));  // open: gt, lt
  Comparator #(.width(6)) comparator_17 (.a(Instruction[31:26]), .b(6'b101011), .eq(sw));  // open: gt, lt
  and and_5 (sub, _00_0000, comparator_13_eq);
  and and_6 (divu, _00_0000, comparator_14_eq);
  and and_7 (\xor , _00_0000, comparator_15_eq);
  and and_8 (mflo, _00_0000, comparator_16_eq);
  Comparator #(.width(6)) comparator_18 (.a(Instruction[31:26]), .b({6{1'b1}}), .eq(_11_1111));  // open: gt, lt
  Comparator #(.width(6)) comparator_19 (.a(Instruction[31:26]), .b(6'b001101), .eq(ori));  // open: gt, lt
  Comparator #(.width(6)) comparator_20 (.a(Instruction[31:26]), .b(6'b000100), .eq(beq));  // open: gt, lt
  Comparator #(.width(6)) comparator_21 (.a(Instruction[31:26]), .b(6'b000001), .eq(bltz));  // open: gt, lt
  Comparator #(.width(6)) comparator_22 (.a(Instruction[5:0]), .b(6'b011000), .eq(comparator_22_eq));  // open: gt, lt
  Comparator #(.width(6)) comparator_23 (.a(Instruction[5:0]), .b(6'b100100), .eq(comparator_23_eq));  // open: gt, lt
  Comparator #(.width(6)) comparator_24 (.a(Instruction[5:0]), .b(6'b101010), .eq(comparator_24_eq));  // open: gt, lt
  Comparator #(.width(6)) comparator_25 (.a(Instruction[5:0]), .b({6{1'b0}}), .eq(comparator_25_eq));  // open: gt, lt
  and and_9 (mult, _00_0000, comparator_22_eq);
  and and_10 (\and , _00_0000, comparator_23_eq);
  and and_11 (slt, _00_0000, comparator_24_eq);
  and and_12 (nop, _00_0000, comparator_25_eq);
  Comparator #(.width(6)) comparator_26 (.a(Instruction[31:26]), .b(6'b000010), .eq(j));  // open: gt, lt
  Comparator #(.width(6)) comparator_27 (.a(Instruction[31:26]), .b(6'b001110), .eq(xori));  // open: gt, lt
  Comparator #(.width(6)) comparator_28 (.a(Instruction[31:26]), .b(6'b000101), .eq(bne));  // open: gt, lt
  Comparator #(.width(6)) comparator_29 (.a(Instruction[31:26]), .b(6'b100011), .eq(lw));  // open: gt, lt
  and and_13 (mulu, _00_0000, comparator_30_eq);
  Comparator #(.width(6)) comparator_30 (.a(Instruction[5:0]), .b(6'b011001), .eq(comparator_30_eq));  // open: gt, lt
  and and_14 (\or , _00_0000, comparator_31_eq);
  Comparator #(.width(6)) comparator_31 (.a(Instruction[5:0]), .b(6'b100101), .eq(comparator_31_eq));  // open: gt, lt
  and and_15 (sltu, _00_0000, comparator_32_eq);
  Comparator #(.width(6)) comparator_32 (.a(Instruction[5:0]), .b(6'b101011), .eq(comparator_32_eq));  // open: gt, lt
  and and_16 (jr, _00_0000, comparator_33_eq);
  Comparator #(.width(6)) comparator_33 (.a(Instruction[5:0]), .b(6'b001000), .eq(comparator_33_eq));  // open: gt, lt
  or or_1 (or_1_out, addi, andi, ori, xori, slti);
  or or_2 (or_2_out, sltiu, beq, bne);
  or or_3 (or_3_out, blez, bgtz, bltz, lw, sw);
  or or_4 (Tyoe_I, or_1_out, or_2_out, or_3_out);
  Comparator #(.width(6)) comparator_34 (.a(Instruction[5:0]), .b({6{1'b0}}), .eq(comparator_34_eq));  // open: gt, lt
  Comparator #(.width(6)) comparator_35 (.a(Instruction[5:0]), .b(6'b000001), .eq(comparator_35_eq));  // open: gt, lt
  Comparator #(.width(6)) comparator_36 (.a(Instruction[5:0]), .b({6{1'b1}}), .eq(comparator_36_eq));  // open: gt, lt
  Comparator #(.width(6)) comparator_37 (.a(Instruction[5:0]), .b(6'b000001), .eq(comparator_37_eq));  // open: gt, lt
  Comparator #(.width(6)) comparator_38 (.a(Instruction[5:0]), .b(6'b000010), .eq(comparator_38_eq));  // open: gt, lt
  Comparator #(.width(6)) comparator_39 (.a(Instruction[5:0]), .b(6'b000100), .eq(comparator_39_eq));  // open: gt, lt
  and and_17 (pop, comparator_34_eq, _11_1000);
  and and_18 (push, _11_1000, comparator_35_eq);
  and and_19 (halt, _11_1111, comparator_36_eq);
  and and_20 (tty, _11_1111, comparator_37_eq);
  and and_21 (rnd, _11_1111, comparator_38_eq);
  and and_22 (kbd, _11_1111, comparator_39_eq);

  assign cte = Instruction[15:0];
  assign jump = Instruction[25:0];
  assign Rd = Instruction[15:11];
  assign Rs = Instruction[25:21];
  assign Rt = Instruction[20:16];

  // Other names for the same wires on the sheet: func__code[5:0] = Instruction[5:0];
  //   op__code[5:0] = Instruction[31:26]

  // Notes on the sheet:
  //   op. code: 00 0000
  //   Type R 
  //   op. code: 11 1000
  //   op. code: 11 1111
  //   Type I
  //   --------
  //   Type J
  //   --------
endmodule

module Register_File_Input (
  input  Random,
  input  [31:0] RAM,
  input  Kbd,
  input  Move_From_High,
  input  [31:0] ALU_Output,
  input  Move_From_Low,
  input  [6:0] Keyboard,
  input  Pop,
  input  Load_Word,
  input  Clock,
  input  [31:0] High,
  input  Keyboard_Avail,
  input  [31:0] Low,
  output [31:0] RF_INPUT
);

  wire ram_t;
  wire [2:0] Selector;
  wire [31:0] KBD_In, random_t;

  Random #(.width(32)) u_Random (.clk(Clock), .next(Random), .out(random_t));  // open: clr
  or or_1 (ram_t, Pop, Load_Word);
  or or_2 (Selector[0], Kbd, ram_t, Move_From_Low);
  or or_3 (Selector[1], Random, ram_t);
  or or_4 (Selector[2], Move_From_High, Move_From_Low);
  Multiplexer #(.width(32), .enable("false")) multiplexer_1 (
    .in0({32{1'b1}}), .in1({{25{1'b0}}, Keyboard}), .out(KBD_In), .sel(Keyboard_Avail));
  Multiplexer #(.select(3), .width(32), .enable("false")) multiplexer_2 (
    .in0(ALU_Output), .in1(KBD_In), .in2(random_t), .in3(RAM), .in4(High), .in5(Low), .out(RF_INPUT),
    .sel(Selector));  // open: in6, in7

  // Other names for the same wires on the sheet: ALU[31:0] = ALU_Output; KBD_Avail = Keyboard_Avail;
  //   KBD_t[6:0] = Keyboard; Keyboard_t = Kbd; LW = Load_Word; MFHI = Move_From_High; MFLO = Move_From_Low
endmodule

module Register_File (
  input  [4:0] Data_Address,
  input  [31:0] Data_In,
  input  [31:0] High,
  input  Read_Write,
  input  [4:0] Select_A,
  input  [4:0] Select_B,
  input  Clock,
  input  Reset,
  input  Enable_HL,
  input  Push,
  input  Pop,
  input  Enable_Program_Counter,
  output [31:0] Output_A,
  output [31:0] Output_B,
  output [31:0] High_2,
  output [31:0] Low,
  output [31:0] Stack_Pointer
);

  wire and_1_out, E01, E02, E03, E04, E05, E06, E07, E08, E09, E10, E11, E12, E13, E14, E15, E16, E17, E18,
       E19, E20, E21, E22, E23, E24, E25, E26, E27, E28, E29, E30, E31, Enable_Stack_Pointer, or_1_out;
  wire [31:0] multiplexer_1_out, Out00, Out01, Out02, Out03, Out04, Out05, Out06, Out07, Out08, Out09, Out10,
       Out11, Out12, Out13, Out14, Out15, Out16, Out17, Out18, Out19, Out20, Out21, Out22, Out23, Out24,
       Out25, Out26, Out27, Out28, Out29, Out30, SP___4, SP___4_t, Stack_Pointer_Input;

  Demultiplexer #(.select(5), .enable("false")) demultiplexer_1 (
    .out1(E01), .out2(E02), .out3(E03), .out4(E04), .out5(E05), .out6(E06), .out7(E07), .out8(E08),
    .out9(E09), .out10(E10), .out11(E11), .out12(E12), .out13(E13), .out14(E14), .out15(E15), .out16(E16),
    .out17(E17), .out18(E18), .out19(E19), .out20(E20), .out21(E21), .out22(E22), .out23(E23), .out24(E24),
    .out25(E25), .out26(E26), .out27(E27), .out28(E28), .out29(E29), .out30(E30), .out31(E31),
    .in(Read_Write), .sel(Data_Address));  // open: out0
  Register #(.width(32)) R00 (.D({32{1'b0}}), .Q(Out00), .clk(Clock), .clr(Reset));  // open: en
  Register #(.width(32)) R04 (.D(Data_In), .en(E04), .Q(Out04), .clk(Clock), .clr(Reset));
  Register #(.width(32)) R08 (.D(Data_In), .en(E08), .Q(Out08), .clk(Clock), .clr(Reset));
  Register #(.width(32)) R12 (.D(Data_In), .en(E12), .Q(Out12), .clk(Clock), .clr(Reset));
  Register #(.width(32)) R16 (.D(Data_In), .en(E16), .Q(Out16), .clk(Clock), .clr(Reset));
  Register #(.width(32)) R20 (.D(Data_In), .en(E20), .Q(Out20), .clk(Clock), .clr(Reset));
  Register #(.width(32)) R24 (.D(Data_In), .en(E24), .Q(Out24), .clk(Clock), .clr(Reset));
  Register #(.width(32)) R28 (.D(Data_In), .en(E28), .Q(Out28), .clk(Clock), .clr(Reset));
  Register #(.width(32)) R01 (.D(Data_In), .en(E01), .Q(Out01), .clk(Clock), .clr(Reset));
  Register #(.width(32)) R05 (.D(Data_In), .en(E05), .Q(Out05), .clk(Clock), .clr(Reset));
  Register #(.width(32)) R09 (.D(Data_In), .en(E09), .Q(Out09), .clk(Clock), .clr(Reset));
  Register #(.width(32)) R13 (.D(Data_In), .en(E13), .Q(Out13), .clk(Clock), .clr(Reset));
  Register #(.width(32)) R17 (.D(Data_In), .en(E17), .Q(Out17), .clk(Clock), .clr(Reset));
  Register #(.width(32)) R21 (.D(Data_In), .en(E21), .Q(Out21), .clk(Clock), .clr(Reset));
  Register #(.width(32)) R25 (.D(Data_In), .en(E25), .Q(Out25), .clk(Clock), .clr(Reset));
  Register #(.width(32)) R29 (.D(Data_In), .en(E29), .Q(Out29), .clk(Clock), .clr(Reset));
  Register #(.width(32)) R02 (.D(Data_In), .en(E02), .Q(Out02), .clk(Clock), .clr(Reset));
  Register #(.width(32)) R06 (.D(Data_In), .en(E06), .Q(Out06), .clk(Clock), .clr(Reset));
  Register #(.width(32)) R10 (.D(Data_In), .en(E10), .Q(Out10), .clk(Clock), .clr(Reset));
  Register #(.width(32)) R14 (.D(Data_In), .en(E14), .Q(Out14), .clk(Clock), .clr(Reset));
  Register #(.width(32)) R18 (.D(Data_In), .en(E18), .Q(Out18), .clk(Clock), .clr(Reset));
  Register #(.width(32)) R22 (.D(Data_In), .en(E22), .Q(Out22), .clk(Clock), .clr(Reset));
  Register #(.width(32)) R26 (.D(Data_In), .en(E26), .Q(Out26), .clk(Clock), .clr(Reset));
  Register #(.width(32)) R30 (.D(Data_In), .en(E30), .Q(Out30), .clk(Clock), .clr(Reset));
  Register #(.width(32)) u_HIGH (.D(High), .en(Enable_HL), .Q(High_2), .clk(Clock), .clr(Reset));
  Multiplexer #(.width(32), .enable("false")) multiplexer_1 (
    .in0(SP___4_t), .in1(SP___4), .out(multiplexer_1_out), .sel(Pop));
  Register #(.width(32)) R03 (.D(Data_In), .en(E03), .Q(Out03), .clk(Clock), .clr(Reset));
  Register #(.width(32)) R07 (.D(Data_In), .en(E07), .Q(Out07), .clk(Clock), .clr(Reset));
  Register #(.width(32)) R11 (.D(Data_In), .en(E11), .Q(Out11), .clk(Clock), .clr(Reset));
  Register #(.width(32)) R15 (.D(Data_In), .en(E15), .Q(Out15), .clk(Clock), .clr(Reset));
  Register #(.width(32)) R19 (.D(Data_In), .en(E19), .Q(Out19), .clk(Clock), .clr(Reset));
  Register #(.width(32)) R23 (.D(Data_In), .en(E23), .Q(Out23), .clk(Clock), .clr(Reset));
  Register #(.width(32)) R27 (.D(Data_In), .en(E27), .Q(Out27), .clk(Clock), .clr(Reset));
  Register #(.width(32)) u_LOW (.D(Data_In), .en(Enable_HL), .Q(Low), .clk(Clock), .clr(Reset));
  Multiplexer #(.width(32), .enable("false")) multiplexer_2 (
    .in0(multiplexer_1_out), .in1(Data_In), .out(Stack_Pointer_Input), .sel(E31));
  or or_1 (or_1_out, Push, Pop);
  and and_1 (and_1_out, or_1_out, Enable_Program_Counter);
  Adder #(.width(32)) adder_1 (.a(Stack_Pointer), .b(32'h4), .out(SP___4));  // open: cin, cout
  Register #(.width(32)) SP (
    .D(Stack_Pointer_Input), .en(Enable_Stack_Pointer), .Q(Stack_Pointer), .clk(Clock), .clr(Reset));
  or or_2 (Enable_Stack_Pointer, Reset, and_1_out, E31);
  Subtractor #(.width(32)) subtractor_1 (.a(Stack_Pointer), .b(32'h4), .out(SP___4_t));  // open: bin, bout
  Multiplexer #(.select(5), .width(32), .enable("false")) multiplexer_3 (
    .in0(Out00), .in1(Out01), .in2(Out02), .in3(Out03), .in4(Out04), .in5(Out05), .in6(Out06), .in7(Out07),
    .in8(Out08), .in9(Out09), .in10(Out10), .in11(Out11), .in12(Out12), .in13(Out13), .in14(Out14),
    .in15(Out15), .in16(Out16), .in17(Out17), .in18(Out18), .in19(Out19), .in20(Out20), .in21(Out21),
    .in22(Out22), .in23(Out23), .in24(Out24), .in25(Out25), .in26(Out26), .in27(Out27), .in28(Out28),
    .in29(Out29), .in30(Out30), .in31(Stack_Pointer), .out(Output_A), .sel(Select_A));
  Multiplexer #(.select(5), .width(32), .enable("false")) multiplexer_4 (
    .in0(Out00), .in1(Out01), .in2(Out02), .in3(Out03), .in4(Out04), .in5(Out05), .in6(Out06), .in7(Out07),
    .in8(Out08), .in9(Out09), .in10(Out10), .in11(Out11), .in12(Out12), .in13(Out13), .in14(Out14),
    .in15(Out15), .in16(Out16), .in17(Out17), .in18(Out18), .in19(Out19), .in20(Out20), .in21(Out21),
    .in22(Out22), .in23(Out23), .in24(Out24), .in25(Out25), .in26(Out26), .in27(Out27), .in28(Out28),
    .in29(Out29), .in30(Out30), .in31(Stack_Pointer), .out(Output_B), .sel(Select_B));

  // Other names for the same wires on the sheet: E_HL = Enable_HL; E_PC = Enable_Program_Counter;
  //   High_Input[31:0] = High; High_t[31:0] = High_2; R_W = Read_Write

  // Notes on the sheet:
  //   Inputs
  //   Outputs
endmodule

module ALU (
  input  [31:0] A_Data,
  input  [31:0] B_Data,
  input  [3:0] Selector,
  input  Clock,
  output [31:0] ALU_Output,
  output [31:0] High,
  output Zero_Flag,
  output Negative_Flag
);

  wire SLT_bit, SLTU_bit;
  wire [1:0] Mini_Selector;
  wire [31:0] ADD, AND, DivHigh, DivLow, DivuHigh, DivuLow, Low, Mult_High, Mult_Low, Mulu_High, Mulu_Low,
       NOR, Operations, OR, SLT, SLTU, SUBSTRACT, XOR;

  Adder #(.width(32)) adder_1 (.a(A_Data), .b(B_Data), .out(ADD));  // open: cin, cout
  Multiplier #(.width(32)) multiplier_1 (.a(A_Data), .b(B_Data), .out(Mulu_Low), .cout(Mulu_High));  // open: cin
  Mul mul_1 (.A(A_Data), .B(B_Data), .Low(Mult_Low), .High(Mult_High));
  Comparator #(.width(32)) comparator_1 (.a(A_Data), .b(B_Data), .lt(SLT_bit));  // open: gt, eq
  assign SLT = {{31{1'b0}}, SLT_bit};  // Bit_Extender bit_extender_1
  Subtractor #(.width(32)) subtractor_1 (.a(A_Data), .b(B_Data), .out(SUBSTRACT));  // open: bin, bout
  Divider #(.width(32)) divider_1 (.a(A_Data), .b(B_Data), .out(DivuLow), .rem(DivuHigh));  // open: upper
  Div div_1 (.in_1(A_Data), .in_2(B_Data), .Low(DivLow), .High(DivHigh));
  Comparator #(.width(32), .mode("unsigned")) comparator_2 (.a(A_Data), .b(B_Data), .lt(SLTU_bit));  // open: gt, eq
  assign SLTU = {{31{1'b0}}, SLTU_bit};  // Bit_Extender bit_extender_2
  or or_1 (Mini_Selector[0], Selector[1], Selector[2]);
  or or_2 (Mini_Selector[1], Selector[0], Selector[2]);
  Multiplexer #(.select(3), .width(32), .enable("false")) multiplexer_1 (
    .in0(ADD), .in1(SUBSTRACT), .in2(SLT), .in3(SLTU), .in4(AND), .in5(OR), .in6(NOR), .in7(XOR),
    .out(Operations), .sel(Selector[2:0]));
  assign AND = A_Data & B_Data;  // AND_Gate and_1, 32 bits wide
  assign OR = A_Data | B_Data;  // OR_Gate or_3, 32 bits wide
  assign NOR = ~(A_Data | B_Data);  // NOR_Gate nor_1, 32 bits wide
  assign XOR = A_Data ^ B_Data;  // XOR_Gate xor_1, 32 bits wide
  Multiplexer #(.width(32), .enable("false")) multiplexer_2 (
    .in0(Operations), .in1(Low), .out(ALU_Output), .sel(Selector[3]));
  Comparator #(.width(32)) comparator_3 (
    .a(ALU_Output), .b({32{1'b0}}), .eq(Zero_Flag), .lt(Negative_Flag));  // open: gt
  Multiplexer #(.select(2), .width(32), .enable("false")) multiplexer_3 (
    .in0(Mult_Low), .in1(DivLow), .in2(Mulu_Low), .in3(DivuLow), .out(Low), .sel(Mini_Selector));
  Multiplexer #(.select(2), .width(32), .enable("false")) multiplexer_4 (
    .in0(Mult_High), .in1(DivHigh), .in2(Mulu_High), .in3(DivuHigh), .out(High), .sel(Mini_Selector));

  // Other names for the same wires on the sheet: A[31:0] = A_Data; B[31:0] = B_Data; Output[31:0] = ALU_Output;
  //   Selector_t[2:0] = Selector[2:0]; Enable = Selector[3]

  // Notes on the sheet:
  //   INPUTS
  //   ARITHMETIC
  //   LOGIC
  //   OUTPUTS
endmodule

module ALU_Encoder (
  input  add,
  input  \and ,
  input  slt,
  input  addi,
  input  andi,
  input  slti,
  input  \or ,
  input  sub,
  input  sltu,
  input  orii,
  input  sltui,
  input  div,
  input  mult,
  input  \xor ,
  input  \nor ,
  input  divu,
  input  xorii,
  input  multu,
  output [3:0] ALU_Selector
);

  wire add_t, and_t, or_t, slt_t, sltu_t, xor_t;

  or or_1 (add_t, add, addi);
  or or_2 (ALU_Selector[0], sub, sltu_t, xor_t, or_t, multu);
  or or_3 (ALU_Selector[1], slt_t, sltu_t, \nor , xor_t, div);
  or or_4 (and_t, \and , andi);
  or or_5 (or_t, \or , orii);
  or or_6 (xor_t, \xor , xorii);
  or or_7 (ALU_Selector[2], and_t, or_t, \nor , xor_t, divu);
  or or_8 (ALU_Selector[3], mult, multu, div, divu);
  or or_9 (slt_t, slt, slti);
  or or_10 (sltu_t, sltu, sltui);

  // Other names for the same wires on the sheet: _0 = ALU_Selector[0]; _1 = ALU_Selector[1]; _2 = ALU_Selector[2];
  //   _3 = ALU_Selector[3]; ori = orii; xori = xorii

  // Notes on the sheet:
  //   ALU Operations
endmodule

// sig \n÷
module Div (
  input  [31:0] in_1,
  input  [31:0] in_2,
  output [31:0] Low,
  output [31:0] High
);

  wire Zero;
  wire [1:0] Selector;
  wire [31:0] mul_1_low, multiplexer_1_out, multiplexer_2_out, negative_div, negative_div_t, negator_3_out,
       negator_4_out, positive_div, positive_div_t, rest, val;

  // Probe on in_1
  // Probe on in_2
  Negator #(.width(32)) negator_1 (.in(positive_div_t), .out(positive_div));
  Adder #(.width(32)) adder_1 (.a(positive_div_t), .b(val), .out(negative_div_t));  // open: cin, cout
  Negator #(.width(32)) negator_2 (.in(negative_div_t), .out(negative_div));
  Negator #(.width(32)) negator_3 (.in(in_1), .out(negator_3_out));
  Comparator #(.width(1)) comparator_1 (.a(1'b1), .b(in_1[31]), .eq(Selector[1]));  // open: gt, lt
  Negator #(.width(32)) negator_4 (.in(in_2), .out(negator_4_out));
  Comparator #(.width(1)) comparator_2 (.a(1'b1), .b(in_2[31]), .eq(Selector[0]));  // open: gt, lt
  Comparator #(.width(32)) comparator_3 (.a({32{1'b0}}), .b(rest), .eq(Zero));  // open: gt, lt
  Multiplexer #(.width(32), .enable("false")) multiplexer_1 (
    .in0(in_1), .in1(negator_3_out), .out(multiplexer_1_out), .sel(Selector[1]));
  Multiplexer #(.width(32), .enable("false")) multiplexer_2 (
    .in0(in_2), .in1(negator_4_out), .out(multiplexer_2_out), .sel(Selector[0]));
  Multiplexer #(.width(32), .enable("false")) multiplexer_3 (.in0(32'h1), .in1({32{1'b0}}), .out(val), .sel(Zero));
  Divider #(.width(32)) divider_1 (
    .a(multiplexer_1_out), .b(multiplexer_2_out), .out(positive_div_t), .rem(rest));  // open: upper
  Mul mul_1 (.A(in_2), .B(Low), .Low(mul_1_low));  // open: High
  Multiplexer #(.select(2), .width(32), .enable("false")) multiplexer_4 (
    .in0(positive_div_t), .in1(positive_div), .in2(negative_div), .in3(negative_div_t), .out(Low),
    .sel(Selector));
  // Probe on Low
  Subtractor #(.width(32)) subtractor_1 (.a(in_1), .b(mul_1_low), .out(High));  // open: bin, bout
  // Probe on High

  // Other names for the same wires on the sheet: A[31:0] = in_1; B[31:0] = in_2; result[31:0] = Low;
  //   SelectorB = Selector[0]; SelectorA = Selector[1]

  // Notes on the sheet:
  //   A
  //   B
endmodule

// sig \n×
module Mul (
  input  [31:0] A,
  input  [31:0] B,
  output [31:0] Low,
  output [31:0] High
);

  wire Carry_Low, Negative_Out, Selector_A, Selector_B;
  wire [31:0] adder_1_out, adder_2_out, bit_negator_1_output, bit_negator_2_output, multiplexer_1_out,
       multiplexer_2_out, multiplier_1_cout, multiplier_1_out, negator_1_out, negator_2_out;

  // Probe on A
  // Probe on B
  Comparator #(.width(1)) comparator_1 (.a(1'b1), .b(A[31]), .eq(Selector_A));  // open: gt, lt
  Negator #(.width(32)) negator_1 (.in(A), .out(negator_1_out));
  Negator #(.width(32)) negator_2 (.in(B), .out(negator_2_out));
  Comparator #(.width(1)) comparator_2 (.a(B[31]), .b(1'b1), .eq(Selector_B));  // open: gt, lt
  Multiplexer #(.width(32), .enable("false")) multiplexer_1 (
    .in0(A), .in1(negator_1_out), .out(multiplexer_1_out), .sel(Selector_A));
  Multiplexer #(.width(32), .enable("false")) multiplexer_2 (
    .in0(B), .in1(negator_2_out), .out(multiplexer_2_out), .sel(Selector_B));
  Multiplier #(.width(32)) multiplier_1 (
    .a(multiplexer_1_out), .b(multiplexer_2_out), .out(multiplier_1_out), .cout(multiplier_1_cout));  // open: cin
  xor xor_1 (Negative_Out, Selector_A, Selector_B);
  Bit_Negator bit_negator_1 (.Number(multiplier_1_out), .Output(bit_negator_1_output));
  Bit_Negator bit_negator_2 (.Number(multiplier_1_cout), .Output(bit_negator_2_output));
  Adder #(.width(32)) adder_1 (.a(bit_negator_1_output), .b(32'h1), .out(adder_1_out), .cout(Carry_Low));  // open: cin
  Adder #(.width(32)) adder_2 (
    .a(bit_negator_2_output), .b({32{1'b0}}), .out(adder_2_out), .cin(Carry_Low));  // open: cout
  Multiplexer #(.width(32), .enable("false")) multiplexer_3 (
    .in0(multiplier_1_out), .in1(adder_1_out), .out(Low), .sel(Negative_Out));
  Multiplexer #(.width(32), .enable("false")) multiplexer_4 (
    .in0(multiplier_1_cout), .in1(adder_2_out), .out(High), .sel(Negative_Out));
  // Probe on Low
  // Probe on High
endmodule

module Branch_Control (
  input  Branch_If_Equal,
  input  [31:0] Program_Counter,
  input  Branch_If_Not_Equal,
  input  Branch_If__Less_Equal_Zero,
  input  [15:0] Constant,
  input  Branch_If_Greater_Than_Zero,
  input  Branch_If_Less_Than_Zero,
  input  [25:0] Jump,
  input  j,
  input  Jump_Register,
  input  [31:0] Source_Registration_1,
  input  [31:0] Source_Registration_2,
  output [31:0] Next_Instruction
);

  wire and_1_out, and_2_out, and_3_out, and_4_out, and_5_out, not_1_out, or_1_out, or_2_out, SR1___0,
       SR1____0, SR1____SR2;
  wire [1:0] Selector;
  wire [31:0] PC___4, PC___4___4___Offset;
  wire [31:18] _4___Offset;

  or or_1 (or_1_out, SR1____0, SR1___0);
  not not_1 (not_1_out, or_1_out);
  and and_1 (and_1_out, Branch_If_Equal, SR1____SR2);
  and and_2 (and_2_out, ~SR1____SR2, Branch_If_Not_Equal);  // AND_Gate
  and and_3 (and_3_out, Branch_If__Less_Equal_Zero, or_1_out);
  and and_4 (and_4_out, not_1_out, Branch_If_Greater_Than_Zero);
  and and_5 (and_5_out, Branch_If_Less_Than_Zero, SR1___0);
  or or_2 (or_2_out, and_1_out, and_2_out, and_3_out, and_4_out, and_5_out);
  assign _4___Offset = {{13{Constant[15]}}, Constant[15]};  // Bit_Extender bit_extender_1
  Adder #(.width(32)) adder_1 (.a(Program_Counter), .b(32'h4), .out(PC___4));  // open: cin, cout
  Adder #(.width(32)) adder_2 (
    .a(PC___4), .b({_4___Offset, Constant, 2'b00}), .out(PC___4___4___Offset));  // open: cin, cout
  Comparator #(.width(32)) comparator_1 (
    .a(Source_Registration_1), .b(Source_Registration_2), .eq(SR1____SR2));  // open: gt, lt
  or or_3 (Selector[0], j, Jump_Register);
  or or_4 (Selector[1], or_2_out, Jump_Register);
  Comparator #(.width(32)) comparator_2 (
    .a(Source_Registration_1), .b({32{1'b0}}), .eq(SR1____0), .lt(SR1___0));  // open: gt
  Multiplexer #(.select(2), .width(32), .enable("false")) multiplexer_1 (
    .in0(PC___4), .in1({Program_Counter[31:28], Jump, 2'b00}), .in2(PC___4___4___Offset),
    .in3(Source_Registration_1), .out(Next_Instruction), .sel(Selector));

  // Other names for the same wires on the sheet: _4___Offset[17:2] = Constant; CTE[15:0] = Constant;
  //   BEQ = Branch_If_Equal; BGTZ = Branch_If_Greater_Than_Zero; BLEZ = Branch_If__Less_Equal_Zero;
  //   BLTZ = Branch_If_Less_Than_Zero; BNE = Branch_If_Not_Equal; JR = Jump_Register;
  //   Jump_Destiny[31:2] = {Program_Counter[31:28], Jump}; PC[31:0] = Program_Counter;
  //   SR1[31:0] = Source_Registration_1; SR2[31:0] = Source_Registration_2
endmodule

module Program_Counter (
  input  [31:0] Branch_Control,
  input  Clock,
  input  Enabled,
  input  Reset,
  output [31:0] Instruction
);

  Register #(.width(32)) Program_Counter (.D(Branch_Control), .en(Enabled), .Q(Instruction), .clk(Clock), .clr(Reset));
endmodule

// RAM\ Read /Write
module RAM_Address (
  input  [31:0] ALU,
  input  [31:0] Stack_Pointer,
  input  [31:0] Program_Counter,
  input  Store_Word,
  input  Load_Word,
  input  Pop,
  input  Push,
  input  Program_Counter_Address,
  output [31:0] Dir_RAM
);

  wire [1:0] Selector;
  wire [31:0] multiplexer_1_out, subtractor_1_out;

  Subtractor #(.width(32)) subtractor_1 (.a(Stack_Pointer), .b(32'h4), .out(subtractor_1_out));  // open: bin, bout
  or or_1 (Selector[1], Pop, Program_Counter_Address, Push);
  or or_2 (Selector[0], Store_Word, Program_Counter_Address, Load_Word);
  Multiplexer #(.width(32), .enable("false")) multiplexer_1 (
    .in0(Stack_Pointer), .in1(subtractor_1_out), .out(multiplexer_1_out), .sel(Push));
  Multiplexer #(.select(2), .width(32), .enable("false")) multiplexer_2 (
    .in0(Program_Counter), .in1(ALU), .in2(multiplexer_1_out), .in3(Program_Counter), .out(Dir_RAM),
    .sel(Selector));

  // Other names for the same wires on the sheet: LW = Load_Word; PC[31:0] = Program_Counter;
  //   PC_Address = Program_Counter_Address; SP[31:0] = Stack_Pointer; SW = Store_Word
endmodule

module Bit_Negator (
  input  [31:0] Number,
  output [31:0] Output
);

  not not_1 (Output[0], Number[0]);
  not not_2 (Output[1], Number[1]);
  not not_3 (Output[2], Number[2]);
  not not_4 (Output[3], Number[3]);
  not not_5 (Output[4], Number[4]);
  not not_6 (Output[5], Number[5]);
  not not_7 (Output[6], Number[6]);
  not not_8 (Output[7], Number[7]);
  not not_9 (Output[8], Number[8]);
  not not_10 (Output[9], Number[9]);
  not not_11 (Output[10], Number[10]);
  not not_12 (Output[11], Number[11]);
  not not_13 (Output[12], Number[12]);
  not not_14 (Output[13], Number[13]);
  not not_15 (Output[14], Number[14]);
  not not_16 (Output[15], Number[15]);
  not not_17 (Output[16], Number[16]);
  not not_18 (Output[17], Number[17]);
  not not_19 (Output[18], Number[18]);
  not not_20 (Output[19], Number[19]);
  not not_21 (Output[20], Number[20]);
  not not_22 (Output[21], Number[21]);
  not not_23 (Output[22], Number[22]);
  not not_24 (Output[23], Number[23]);
  not not_25 (Output[24], Number[24]);
  not not_26 (Output[25], Number[25]);
  not not_27 (Output[26], Number[26]);
  not not_28 (Output[27], Number[27]);
  not not_29 (Output[28], Number[28]);
  not not_30 (Output[29], Number[29]);
  not not_31 (Output[30], Number[30]);
  not not_32 (Output[31], Number[31]);
endmodule

// Read \n From \n RAM
module Read_From_RAM (
  input  [31:0] RAM_Address,
  input  [31:0] Bank_0,
  input  [31:0] Bank_1,
  input  [31:0] Bank_2,
  input  [31:0] Bank_3,
  output [31:0] Value
);

  wire [31:0] multiplexer_1_out;

  Multiplexer #(.select(2), .width(32), .enable("false")) multiplexer_1 (
    .in0(Bank_0), .in1(Bank_1), .in2(Bank_2), .in3(Bank_3), .out(multiplexer_1_out), .sel(RAM_Address[3:2]));
  Little_Endian_to_Big_Endian little_endian_to_big_endian_1 (.Instruction(multiplexer_1_out), .Output(Value));

  // Other names for the same wires on the sheet: Selector[1:0] = RAM_Address[3:2]
endmodule

// LETBE
module Little_Endian_to_Big_Endian (
  input  [31:0] Instruction,
  output [31:0] Output
);


  assign Output = {Instruction[7:0], Instruction[15:8], Instruction[23:16], Instruction[31:24]};
endmodule

// Write \n To \n RAM
module Write_To_RAM (
  input  [31:0] RAM_Address,
  input  [31:0] Value,
  output [15:0] ADDR,
  output [3:0] Mask,
  output [31:0] Bank_0,
  output [31:0] Bank_1,
  output [31:0] Bank_2,
  output [31:0] Bank_3
);

  wire [31:0] little_endian_to_big_endian_1_output;

  Little_Endian_to_Big_Endian little_endian_to_big_endian_1 (
    .Instruction(Value), .Output(little_endian_to_big_endian_1_output));
  Demultiplexer #(.select(2), .width(32), .enable("false")) demultiplexer_1 (
    .out0(Bank_0), .out1(Bank_1), .out2(Bank_2), .out3(Bank_3), .in(little_endian_to_big_endian_1_output),
    .sel(RAM_Address[3:2]));
  Demultiplexer #(.select(2), .enable("false")) demultiplexer_2 (
    .out0(Mask[0]), .out1(Mask[1]), .out2(Mask[2]), .out3(Mask[3]), .in(1'b1), .sel(RAM_Address[3:2]));

  assign ADDR = RAM_Address[19:4];

  // Other names for the same wires on the sheet: Selector[1:0] = RAM_Address[3:2]
endmodule
